// Digital circuit LookAhead.dig as structural Verilog
module LookAhead (
  input  [3:0] g,
  input  [3:0] p,
  input  C_i,
  output [3:0] C_o,
  output P_2,
  output G_2
);

  wire or_2_out, or_3_out, or_4_out, or_5_out, or_6_out, or_7_out, or_8_out, or_9_out, or_10_out, or_11_out;

  or or_1 (P_2, p[0], p[1], p[2], p[3]);
  or or_2 (or_2_out, g[0], p[1], p[2], p[3]);
  or or_3 (or_3_out, g[1], p[2], p[3]);
  or or_4 (or_4_out, p[3], g[2]);
  or or_5 (or_5_out, p[0], p[1], C_i);
  or or_6 (or_6_out, g[0], p[1]);
  or or_7 (or_7_out, p[2], p[0], C_i, p[1]);
  or or_8 (or_8_out, g[0], p[1], p[2]);
  or or_9 (or_9_out, g[1], p[2]);
  and and_1 (G_2, or_2_out, or_3_out, or_4_out, g[3]);
  or or_10 (or_10_out, p[0], C_i);
  and and_2 (C_o[0], or_10_out, g[0]);
  and and_3 (C_o[1], or_5_out, or_6_out, g[1]);
  and and_4 (C_o[2], or_7_out, or_8_out, g[2], or_9_out);
  or or_11 (or_11_out, P_2, C_i);
  and and_5 (C_o[3], or_11_out, G_2);

  // Other names for the same wires on the sheet: C0 = C_i; g_0 = g[0]; g_1 = g[1]; g_2_t = g[2]; g_3 = g[3];
  //   p_0 = p[0]; p_1 = p[1]; p_2_t = p[2]; p_3 = p[3]
endmodule
