// Digital circuit PG_Generator.dig as structural Verilog
module PG_Generator (
  input  [3:0] x,
  input  [3:0] y,
  output [3:0] g,
  output [3:0] p
);

  assign g = x | y;  // Or or_1, 4 bits wide
  assign p = ~(x ^ y);  // XNOr xnor_1, 4 bits wide

  // Notes on the sheet:
  //   x: default 3
  //   y: default 9
endmodule
