// Digital circuit TwoLevelCLA.dig as structural Verilog
module TwoLevelCLA (
  input  [15:0] X,
  input  [15:0] Y,
  input  Cin,
  output Cout,
  output [15:0] S
);

  wire c_4, c_8, c_12;
  wire [3:0] lookahead_1_g_2, lookahead_1_p_2, lookahead_2_c_o, lookahead_3_c_o, lookahead_4_c_o,
       pg_generator_1_g, pg_generator_1_p, pg_generator_2_g, pg_generator_2_p, pg_generator_3_g,
       pg_generator_3_p, pg_generator_4_g, pg_generator_4_p;
  wire [4:1] lookahead_1_c_o;

  PG_Generator pg_generator_1 (.x(X[3:0]), .y(Y[3:0]), .g(pg_generator_1_g), .p(pg_generator_1_p));
  PG_Generator pg_generator_2 (.x(X[7:4]), .y(Y[7:4]), .g(pg_generator_2_g), .p(pg_generator_2_p));
  PG_Generator pg_generator_3 (.x(X[11:8]), .y(Y[11:8]), .g(pg_generator_3_g), .p(pg_generator_3_p));
  PG_Generator pg_generator_4 (.x(X[15:12]), .y(Y[15:12]), .g(pg_generator_4_g), .p(pg_generator_4_p));
  LookAhead lookahead_1 (
    .g(pg_generator_1_g), .p(pg_generator_1_p), .C_i(Cin), .C_o(lookahead_1_c_o), .P_2(lookahead_1_p_2[0]),
    .G_2(lookahead_1_g_2[0]));
  LookAhead lookahead_2 (
    .g(pg_generator_2_g), .p(pg_generator_2_p), .C_i(c_4), .C_o(lookahead_2_c_o), .P_2(lookahead_1_p_2[1]),
    .G_2(lookahead_1_g_2[1]));
  LookAhead lookahead_3 (
    .g(pg_generator_3_g), .p(pg_generator_3_p), .C_i(c_8), .C_o(lookahead_3_c_o), .P_2(lookahead_1_p_2[2]),
    .G_2(lookahead_1_g_2[2]));
  LookAhead lookahead_4 (
    .g(pg_generator_4_g), .p(pg_generator_4_p), .C_i(c_12), .C_o(lookahead_4_c_o), .P_2(lookahead_1_p_2[3]),
    .G_2(lookahead_1_g_2[3]));
  assign S = ~({pg_generator_4_p, pg_generator_3_p, pg_generator_2_p, pg_generator_1_p} ^ {lookahead_4_c_o[2:0], lookahead_3_c_o, lookahead_2_c_o, lookahead_1_c_o, Cin});  // XNOr xnor_1, 16 bits wide
  LookAhead lookahead_5 (
    .g(lookahead_1_g_2), .p(lookahead_1_p_2), .C_i(Cin), .C_o({Cout, c_12, c_8, c_4}));  // open: P_2, G_2

  // Other names for the same wires on the sheet: c_16 = Cout; c_0 = Cin

  // Notes on the sheet:
  //   X: default 56
  //   Y: default 7
endmodule
